// Logisim project Hack.circ as structural Verilog
module FullAdder (
  input  a,
  input  b,
  input  c,
  output sum,
  output carry
);

  wire halfadder_1_carry, halfadder_1_sum, halfadder_2_carry;

  HalfAdder halfadder_1 (.a(a), .b(b), .sum(halfadder_1_sum), .carry(halfadder_1_carry));
  HalfAdder halfadder_2 (.a(halfadder_1_sum), .b(c), .sum(sum), .carry(halfadder_2_carry));
  or or_1 (carry, halfadder_1_carry, halfadder_2_carry);
endmodule

module HalfAdder (
  input  a,
  input  b,
  output sum,
  output carry
);

  xor xor_1 (sum, a, b);
  and and_1 (carry, a, b);
endmodule

module Add16OLD (
  input  a0,
  input  b0,
  input  a1,
  input  b1,
  input  a2,
  input  b2,
  input  a3,
  input  b3,
  input  a4,
  input  b4,
  input  a5,
  input  b5,
  input  a6,
  input  b6,
  input  a7,
  input  b7,
  input  a8,
  input  b8,
  input  a9,
  input  b9,
  input  a10,
  input  b10,
  input  a11,
  input  b11,
  input  a12,
  input  b12,
  input  a13,
  input  b13,
  input  a14,
  input  b14,
  input  a15,
  input  b15,
  output out0,
  output out1,
  output out2,
  output out3,
  output out4,
  output out5,
  output out6,
  output out7,
  output out8,
  output out9,
  output out10,
  output out11,
  output out12,
  output out13,
  output out14,
  output out15
);

  wire fulladder_1_carry, fulladder_2_carry, fulladder_3_carry, fulladder_4_carry, fulladder_5_carry,
       fulladder_6_carry, fulladder_7_carry, fulladder_8_carry, fulladder_9_carry, fulladder_10_carry,
       fulladder_11_carry, fulladder_12_carry, fulladder_13_carry, fulladder_14_carry, halfadder_1_carry;

  HalfAdder halfadder_1 (.a(a0), .b(b0), .sum(out0), .carry(halfadder_1_carry));
  FullAdder fulladder_1 (.a(a1), .b(b1), .c(halfadder_1_carry), .sum(out1), .carry(fulladder_1_carry));
  FullAdder fulladder_2 (.a(a2), .b(b2), .c(fulladder_1_carry), .sum(out2), .carry(fulladder_2_carry));
  FullAdder fulladder_3 (.a(a3), .b(b3), .c(fulladder_2_carry), .sum(out3), .carry(fulladder_3_carry));
  FullAdder fulladder_4 (.a(a4), .b(b4), .c(fulladder_3_carry), .sum(out4), .carry(fulladder_4_carry));
  FullAdder fulladder_5 (.a(a5), .b(b5), .c(fulladder_4_carry), .sum(out5), .carry(fulladder_5_carry));
  FullAdder fulladder_6 (.a(a6), .b(b6), .c(fulladder_5_carry), .sum(out6), .carry(fulladder_6_carry));
  FullAdder fulladder_7 (.a(a7), .b(b7), .c(fulladder_6_carry), .sum(out7), .carry(fulladder_7_carry));
  FullAdder fulladder_8 (.a(a8), .b(b8), .c(fulladder_7_carry), .sum(out8), .carry(fulladder_8_carry));
  FullAdder fulladder_9 (.a(a9), .b(b9), .c(fulladder_8_carry), .sum(out9), .carry(fulladder_9_carry));
  FullAdder fulladder_10 (.a(a10), .b(b10), .c(fulladder_9_carry), .sum(out10), .carry(fulladder_10_carry));
  FullAdder fulladder_11 (.a(a11), .b(b11), .c(fulladder_10_carry), .sum(out11), .carry(fulladder_11_carry));
  FullAdder fulladder_12 (.a(a12), .b(b12), .c(fulladder_11_carry), .sum(out12), .carry(fulladder_12_carry));
  FullAdder fulladder_13 (.a(a13), .b(b13), .c(fulladder_12_carry), .sum(out13), .carry(fulladder_13_carry));
  FullAdder fulladder_14 (.a(a14), .b(b14), .c(fulladder_13_carry), .sum(out14), .carry(fulladder_14_carry));
  FullAdder fulladder_15 (.a(a15), .b(b15), .c(fulladder_14_carry), .sum(out15));  // open: carry
endmodule

module Mux4Way16 (
  input  [15:0] in0,
  input  [15:0] in1,
  input  [15:0] in2,
  input  [15:0] in3,
  input  sel0,
  input  sel1,
  output [15:0] outPin
);

  wire [15:0] multiplexer_1_out, multiplexer_2_out;

  Multiplexer #(.width(16)) multiplexer_1 (.in0(in0), .in1(in1), .out(multiplexer_1_out), .sel(sel0));
  Multiplexer #(.width(16)) multiplexer_2 (.in0(in2), .in1(in3), .out(multiplexer_2_out), .sel(sel0));
  Multiplexer #(.width(16)) multiplexer_3 (.in0(multiplexer_1_out), .in1(multiplexer_2_out), .out(outPin), .sel(sel1));
endmodule

module ALU (
  input  zx,
  input  nx,
  input  zy,
  input  ny,
  input  f,
  input  no,
  input  [15:0] x,
  input  [15:0] y,
  output [15:0] outPin,
  output zr,
  output ng
);

  wire or16way_1_outpin;
  wire [15:0] add16_1_outpin, and_1_out, multiplexer_1_out, multiplexer_2_out, multiplexer_3_out,
       multiplexer_4_out, multiplexer_5_out, not_1_out, not_2_out, not_3_out;

  // Probe on multiplexer_3_out
  Multiplexer #(.width(16)) multiplexer_1 (.in0(x), .in1({16{1'b0}}), .out(multiplexer_1_out), .sel(zx));
  Multiplexer #(.width(16)) multiplexer_2 (.in0(y), .in1({16{1'b0}}), .out(multiplexer_2_out), .sel(zy));
  Multiplexer #(.width(16)) multiplexer_3 (.in0(multiplexer_1_out), .in1(not_1_out), .out(multiplexer_3_out), .sel(nx));
  assign not_1_out = ~multiplexer_1_out;  // NOT_Gate not_1, 16 bits wide
  Multiplexer #(.width(16)) multiplexer_4 (.in0(multiplexer_2_out), .in1(not_2_out), .out(multiplexer_4_out), .sel(ny));
  assign not_2_out = ~multiplexer_2_out;  // NOT_Gate not_2, 16 bits wide
  // Probe on multiplexer_4_out
  assign and_1_out = multiplexer_3_out & multiplexer_4_out;  // AND_Gate and_1, 16 bits wide
  Add16 add16_1 (.a(multiplexer_3_out), .b(multiplexer_4_out), .outPin(add16_1_outpin));
  Multiplexer #(.width(16)) multiplexer_5 (.in0(and_1_out), .in1(add16_1_outpin), .out(multiplexer_5_out), .sel(f));
  // Probe on multiplexer_5_out
  assign not_3_out = ~multiplexer_5_out;  // NOT_Gate not_3, 16 bits wide
  Multiplexer #(.width(16)) multiplexer_6 (
    .in0(multiplexer_5_out), .in1(not_3_out), .out({ng, outPin[14:0]}), .sel(no));
  // Probe on {ng, outPin[14:0]}
  Or16Way or16way_1 (.inPin({ng, outPin[14:0]}), .outPin(or16way_1_outpin));
  not not_4 (zr, or16way_1_outpin);

  assign outPin[15] = ng;

  // Other names for the same wires on the sheet: readyOut[15:0] = {ng, outPin[14:0]}
endmodule

module DMux8Way (
  input  inPin,
  input  sel2,
  input  sel1,
  input  sel0,
  output a,
  output b,
  output c,
  output d,
  output e,
  output f,
  output g,
  output h
);

  wire demultiplexer_1_out0, demultiplexer_1_out1;

  Demultiplexer demultiplexer_1 (.out0(demultiplexer_1_out0), .out1(demultiplexer_1_out1), .in(inPin), .sel(sel2));
  DMux4Way dmux4way_1 (.inPin(demultiplexer_1_out0), .sel1(sel1), .sel0(sel0), .a(a), .b(b), .c(c), .d(d));
  DMux4Way dmux4way_2 (.inPin(demultiplexer_1_out1), .sel1(sel1), .sel0(sel0), .a(e), .b(f), .c(g), .d(h));
endmodule

module DMux4Way (
  input  inPin,
  input  sel1,
  input  sel0,
  output a,
  output b,
  output c,
  output d
);

  wire demultiplexer_1_out0, demultiplexer_1_out1;

  Demultiplexer demultiplexer_1 (.out0(demultiplexer_1_out0), .out1(demultiplexer_1_out1), .in(inPin), .sel(sel1));
  Demultiplexer demultiplexer_2 (.out0(a), .out1(b), .in(demultiplexer_1_out0), .sel(sel0));
  Demultiplexer demultiplexer_3 (.out0(c), .out1(d), .in(demultiplexer_1_out1), .sel(sel0));
endmodule

module Mux8Way16 (
  input  [15:0] a,
  input  [15:0] b,
  input  [15:0] c,
  input  [15:0] d,
  input  [15:0] e,
  input  [15:0] f,
  input  [15:0] g,
  input  [15:0] h,
  input  sel1,
  input  sel0,
  input  sel2,
  output [15:0] outPin
);

  wire [15:0] mux4way16_1_outpin, mux4way16_2_outpin;

  Mux4Way16 mux4way16_1 (.in0(a), .in1(b), .in2(c), .in3(d), .sel0(sel0), .sel1(sel1), .outPin(mux4way16_1_outpin));
  Mux4Way16 mux4way16_2 (.in0(e), .in1(f), .in2(g), .in3(h), .sel0(sel0), .sel1(sel1), .outPin(mux4way16_2_outpin));
  Multiplexer #(.width(16)) multiplexer_1 (
    .in0(mux4way16_1_outpin), .in1(mux4way16_2_outpin), .out(outPin), .sel(sel2));
endmodule

module Inc16 (
  input  [15:0] inPin,
  output [15:0] outPin
);

  Adder #(.width(16)) adder_1 (.a(inPin), .b(16'h1), .out(outPin));  // open: cin, cout
endmodule

module Add16 (
  input  [15:0] a,
  input  [15:0] b,
  output [15:0] outPin
);

  Adder #(.width(16)) adder_1 (.a(a), .b(b), .out(outPin));  // open: cin, cout
endmodule

module Or16 (
  input  [15:0] a,
  input  [15:0] b,
  output [15:0] outPin
);

  assign outPin = a | b;  // OR_Gate or_1, 16 bits wide
endmodule

module Or8Way (
  input  in0,
  input  in1,
  input  in2,
  input  in3,
  input  in4,
  input  in5,
  input  in6,
  input  in7,
  output outPin
);

  or or_1 (outPin, in0, in1, in2, in3, in4, in5, in6, in7);
endmodule

module Not16 (
  input  [15:0] in_1,
  output [15:0] out_2
);

  assign out_2 = ~in_1;  // NOT_Gate not_1, 16 bits wide
endmodule

module Mux16 (
  input  [15:0] a,
  input  [15:0] outPin,
  input  [15:0] b,
  input  sel
);

  Multiplexer #(.width(16)) multiplexer_1 (.in0(a), .in1(b), .out(outPin), .sel(sel));
endmodule

module Or16Way (
  input  [15:0] inPin,
  output outPin
);

  or or_1 (outPin, inPin[0], inPin[1], inPin[2], inPin[3], inPin[4], inPin[5], inPin[6], inPin[7], inPin[9], inPin[10], inPin[11], inPin[12], inPin[13], inPin[14], inPin[15], inPin[8]);
endmodule

module main (
);

  CPU cpu_1 ();  // open: instruction, inM, reset, outM, writeM, addressM, pcOut
endmodule

module Bit (
  input  inPin,
  input  load,
  input  clock,
  output outPin
);

  wire multiplexer_1_out;

  D_Flip_Flop d_ff_1 (.D(multiplexer_1_out), .clk(clock), .Q(outPin));  // open: Qn, preset, reset
  Multiplexer multiplexer_1 (.in1(inPin), .out(multiplexer_1_out), .sel(load));  // open: in0
endmodule

module RAM8 (
  input  [15:0] data,
  input  load,
  input  clock,
  input  addr2,
  input  addr1,
  input  addr0,
  output [15:0] outPin
);

  wire dmux8way_1_a, dmux8way_1_b, dmux8way_1_c, dmux8way_1_d, dmux8way_1_e, dmux8way_1_f, dmux8way_1_g,
       dmux8way_1_h;
  wire [15:0] mux4way16_1_outpin, mux4way16_2_outpin, register_1_q, register_2_q, register_3_q, register_4_q,
       register_5_q, register_6_q, register_7_q, register_8_q;

  DMux8Way dmux8way_1 (
    .inPin(load), .sel2(addr0), .sel1(addr2), .sel0(addr1), .a(dmux8way_1_a), .b(dmux8way_1_b),
    .c(dmux8way_1_c), .d(dmux8way_1_d), .e(dmux8way_1_e), .f(dmux8way_1_f), .g(dmux8way_1_g), .h(dmux8way_1_h));
  Register #(.width(16)) register_1 (.D(data), .en(dmux8way_1_a), .clk(clock), .Q(register_1_q));  // open: clr
  Register #(.width(16)) register_2 (.D(data), .en(dmux8way_1_b), .clk(clock), .Q(register_2_q));  // open: clr
  Register #(.width(16)) register_3 (.D(data), .en(dmux8way_1_c), .clk(clock), .Q(register_3_q));  // open: clr
  Register #(.width(16)) register_4 (.D(data), .en(dmux8way_1_d), .clk(clock), .Q(register_4_q));  // open: clr
  Register #(.width(16)) register_5 (.D(data), .en(dmux8way_1_e), .clk(clock), .Q(register_5_q));  // open: clr
  Register #(.width(16)) register_6 (.D(data), .en(dmux8way_1_f), .clk(clock), .Q(register_6_q));  // open: clr
  Register #(.width(16)) register_7 (.D(data), .en(dmux8way_1_g), .clk(clock), .Q(register_7_q));  // open: clr
  Register #(.width(16)) register_8 (.D(data), .en(dmux8way_1_h), .clk(clock), .Q(register_8_q));  // open: clr
  Mux4Way16 mux4way16_1 (
    .in0(register_1_q), .in1(register_2_q), .in2(register_3_q), .in3(register_4_q), .sel0(addr1),
    .sel1(addr2), .outPin(mux4way16_1_outpin));
  Mux4Way16 mux4way16_2 (
    .in0(register_5_q), .in1(register_6_q), .in2(register_7_q), .in3(register_8_q), .sel0(addr1),
    .sel1(addr2), .outPin(mux4way16_2_outpin));
  // Probe on mux4way16_2_outpin
  // Probe on mux4way16_1_outpin
  Multiplexer #(.width(16)) multiplexer_1 (
    .in0(mux4way16_1_outpin), .in1(mux4way16_2_outpin), .out(outPin), .sel(addr0));

  // Other names for the same wires on the sheet: clockt = clock; sel0 = addr0; sel1 = addr2; sel2 = addr1
endmodule

module PC (
  input  [15:0] inPins,
  input  clock,
  input  reset,
  input  load,
  input  inc,
  output [15:0] outPins
);

  wire or_1_out, or_2_out;
  wire [15:0] inc16_1_outpin, multiplexer_1_out, multiplexer_2_out;

  Multiplexer #(.width(16)) multiplexer_1 (.in0(inPins), .in1({16{1'b0}}), .out(multiplexer_1_out), .sel(reset));
  or or_1 (or_1_out, reset, load);
  Register #(.width(16)) register_1 (.D(multiplexer_2_out), .en(or_2_out), .clk(clock), .Q(outPins));  // open: clr
  Multiplexer #(.width(16)) multiplexer_2 (
    .in0(inc16_1_outpin), .in1(multiplexer_1_out), .out(multiplexer_2_out), .sel(or_1_out));
  or or_2 (or_2_out, or_1_out, inc);
  Inc16 inc16_1 (.inPin(outPins), .outPin(inc16_1_outpin));
endmodule

module CPU (
  input  [15:0] instruction,
  input  [15:0] inM,
  input  reset,
  output [15:0] outM,
  output writeM,
  output [14:0] addressM,
  output [14:0] pcOut
);

  wire and_1_out, and_2_out, and_3_out, and_4_out, cJEQ, cJGT, cJLT, clock_1_out, jump, neg, not_1_out,
       not_2_out, not_3_out, or_1_out, or_2_out, zero;
  wire [5:0] toALU;
  wire [15:0] D_Register_q, multiplexer_2_out, multiplexer_3_out;
  wire [15:4] multiplexer_1_out;
  wire [15:15] A_Register_q, pc_1_outpins;

  Clock clock_1 (.out(clock_1_out));
  not not_1 (not_1_out, neg);
  and and_1 (and_1_out, not_1_out, not_2_out);
  not not_2 (not_2_out, zero);
  Multiplexer #(.width(16)) multiplexer_1 (
    .in0({16{1'b0}}), .in1(instruction),
    .out({multiplexer_1_out[15:12], toALU, multiplexer_1_out[5:4], writeM, cJLT, cJEQ, cJGT}),
    .sel(instruction[15]));
  not not_3 (not_3_out, multiplexer_1_out[15]);
  Multiplexer #(.width(16)) multiplexer_2 (.in0(outM), .in1(instruction), .out(multiplexer_2_out), .sel(not_3_out));
  or or_1 (or_1_out, not_3_out, multiplexer_1_out[5]);
  and and_2 (and_2_out, cJLT, neg);
  and and_3 (and_3_out, cJEQ, zero);
  and and_4 (and_4_out, and_1_out, cJGT);
  Register #(.width(16)) A_Register (
    .D(multiplexer_2_out), .en(or_1_out), .clk(clock_1_out), .Q({A_Register_q[15], addressM}));  // open: clr
  or or_2 (or_2_out, and_3_out, and_4_out);
  or or_3 (jump, and_2_out, or_2_out);
  Register #(.width(16)) D_Register (
    .D(outM), .en(multiplexer_1_out[4]), .clk(clock_1_out), .Q(D_Register_q));  // open: clr
  Multiplexer #(.width(16)) multiplexer_3 (
    .in0({A_Register_q[15], addressM}), .in1(inM), .out(multiplexer_3_out), .sel(multiplexer_1_out[12]));
  PC pc_1 (
    .inPins({A_Register_q[15], addressM}), .clock(clock_1_out), .reset(reset), .load(jump), .inc(1'b1),
    .outPins({pc_1_outpins[15], pcOut}));
  ALU alu_1 (
    .zx(toALU[0]), .nx(toALU[1]), .zy(toALU[2]), .ny(toALU[3]), .f(toALU[4]), .no(toALU[5]),
    .x(D_Register_q), .y(multiplexer_3_out), .outPin(outM), .zr(zero), .ng(neg));
endmodule
