// Logisim project fulladder.circ as structural Verilog: 2 circuits, main circuit FullAdder
module FullAdder (
  input  a,
  input  b,
  input  c,
  input  in_4,
  input  in_5,
  input  in_6,
  input  in_7,
  input  in_8,
  input  in_9,
  input  in_10,
  input  in_11,
  output sum,
  output carry
);

  wire and_1_out, and_2_out, xor_1_out, xor_2_out;

  and and_1 (and_1_out, in_4, in_4);
  xor xor_1 (xor_1_out, in_4, in_4);
  // Probe on xor_2_out
  xor xor_2 (xor_2_out, in_4, in_4);
  xor xor_3 (xor_2_out, in_4, in_4);
  xor xor_4 (xor_2_out, in_4, in_4);
  and and_2 (and_2_out, in_4, in_4);
  // Probe on and_1_out
  and and_3 (and_1_out, in_4, in_4);
  and and_4 (and_1_out, in_4, in_4);
  // Probe on xor_1_out
  // Probe on xor_2_out
  // Probe on xor_2_out
  // Probe on and_2_out
  // Probe on and_1_out
  // Probe on and_1_out
  HalfAdder halfadder_1 ();  // open: a, b, sum, carry
  // OR_Gate or_1 is placed but not wired
  HalfAdder halfadder_2 ();  // open: a, b, sum, carry

  assign in_5 = in_4;
  assign in_6 = in_4;
  assign in_7 = in_4;
  assign in_8 = in_4;
  assign in_9 = in_4;
  assign in_10 = in_4;
  assign in_11 = in_4;
endmodule

module HalfAdder (
  input  a,
  input  b,
  output sum,
  output carry
);

  xor xor_1 (sum, a, b);
  and and_1 (carry, a, b);
endmodule
