// Logisim project nand2tetris.circ as structural Verilog: 1 circuit, main circuit main
module main (
  input  in_1,
  input  in_2,
  input  in_3,
  input  inPin,
  input  in_5,
  input  [1:0] in_6,
  input  sel1,
  input  sel0,
  input  in_9,
  input  in_10,
  input  [1:0] in_11,
  input  [15:0] in_12,
  input  [15:0] in_13,
  input  [15:0] in_14,
  input  [15:0] in_15,
  input  [15:0] in_16,
  input  [15:0] in_17,
  input  [15:0] in_18,
  input  [15:0] in_19,
  input  [15:0] in_20,
  input  [15:0] in_21,
  input  in_22,
  input  in_23,
  input  [15:0] in_24,
  input  [2:0] in_25,
  input  [15:0] in_26,
  input  in_27,
  input  in_28
);

  wire and_1_out, and_2_out, and_3_out, and_6_out, and_7_out, button_1_out, demultiplexer_1_out0,
       demultiplexer_1_out1, demultiplexer_2_out0, demultiplexer_2_out1, demultiplexer_5_out0,
       demultiplexer_5_out1, demultiplexer_6_out0, demultiplexer_6_out1, dipswitch_1_sw1, dipswitch_2_sw1,
       dipswitch_2_sw2, dipswitch_3_sw1, dipswitch_3_sw2, dipswitch_4_sw1, dipswitch_4_sw2, dipswitch_4_sw3,
       dipswitch_4_sw4, dipswitch_4_sw5, dipswitch_4_sw6, dipswitch_4_sw7, dipswitch_4_sw8, nand_1_out,
       nand_2_out, nand_3_out, not_1_out, not_2_out, not_3_out, not_4_out, or_1_out, or_2_out, or_3_out,
       or_4_out, or_5_out, or_6_out, or_7_out, or_8_out, or_9_out, xor_1_out;
  wire [15:0] multiplexer_1_out, multiplexer_2_out, multiplexer_3_out, multiplexer_4_out;

  DipSwitch #(.number(2)) dipswitch_1 (.sw1(dipswitch_1_sw1));  // open: sw2
  Demultiplexer demultiplexer_1 (.out0(demultiplexer_1_out0), .out1(demultiplexer_1_out1), .in(inPin), .sel(sel1));
  Demultiplexer demultiplexer_2 (.out0(demultiplexer_2_out0), .out1(demultiplexer_2_out1), .in(in_9), .sel(in_10));
  DipSwitch #(.number(2)) dipswitch_2 (.sw1(dipswitch_2_sw1), .sw2(dipswitch_2_sw2));
  DipSwitch #(.number(2)) dipswitch_3 (.sw1(dipswitch_3_sw1), .sw2(dipswitch_3_sw2));
  DipSwitch dipswitch_4 (
    .sw1(dipswitch_4_sw1), .sw2(dipswitch_4_sw2), .sw3(dipswitch_4_sw3), .sw4(dipswitch_4_sw4),
    .sw5(dipswitch_4_sw5), .sw6(dipswitch_4_sw6), .sw7(dipswitch_4_sw7), .sw8(dipswitch_4_sw8));
  Demultiplexer #(.select(2)) demultiplexer_3 (.in(demultiplexer_2_out0), .sel(in_11));  // open: out0, out1, out2, out3
  Demultiplexer #(.select(2)) demultiplexer_4 (.in(demultiplexer_2_out1), .sel(in_11));  // open: out0, out1, out2, out3
  not not_1 (not_1_out, dipswitch_3_sw1);
  not not_2 (not_2_out, dipswitch_3_sw2);
  not not_3 (not_3_out, in_3);
  not not_4 (not_4_out, button_1_out);
  Button button_1 (.out(button_1_out));
  Demultiplexer demultiplexer_5 (
    .out0(demultiplexer_5_out0), .out1(demultiplexer_5_out1), .in(demultiplexer_1_out0), .sel(sel0));
  Demultiplexer demultiplexer_6 (
    .out0(demultiplexer_6_out0), .out1(demultiplexer_6_out1), .in(demultiplexer_1_out1), .sel(sel0));
  xor xor_1 (xor_1_out, in_27, in_28);
  and and_1 (and_1_out, in_27, in_28);
  or or_1 (or_1_out, dipswitch_4_sw1, dipswitch_4_sw2);
  and and_2 (and_2_out, in_1, in_3);
  and and_3 (and_3_out, in_2, not_3_out);
  // AND_Gate and_4 has open pins: in0=dipswitch_1_sw1, in1=button_1_out, out=open
  // AND_Gate and_5 has open pins: in0=dipswitch_1_sw1, in1=not_4_out, out=open
  // Probe on demultiplexer_5_out0
  // Probe on demultiplexer_5_out1
  // Probe on demultiplexer_6_out0
  // Probe on demultiplexer_6_out1
  // Probe on xor_1_out
  // Probe on and_1_out
  nand nand_1 (nand_1_out, dipswitch_2_sw1, dipswitch_2_sw1);
  nand nand_2 (nand_2_out, dipswitch_2_sw2, dipswitch_2_sw2);
  and and_6 (and_6_out, dipswitch_3_sw1, not_2_out);
  and and_7 (and_7_out, not_1_out, dipswitch_3_sw2);
  or or_2 (or_2_out, or_1_out, dipswitch_4_sw3);
  or or_3 (or_3_out, and_2_out, and_3_out);
  Multiplexer #(.width(16)) multiplexer_1 (.in0(in_14), .in1(in_16), .out(multiplexer_1_out), .sel(in_22));
  Multiplexer #(.width(16)) multiplexer_2 (.in0(in_18), .in1(in_21), .out(multiplexer_2_out), .sel(in_22));
  or or_4 (or_4_out, and_6_out, and_7_out);
  or or_5 (or_5_out, or_2_out, dipswitch_4_sw4);
  // Probe on or_3_out
  // Probe on nand_3_out
  nand nand_3 (nand_3_out, nand_1_out, nand_2_out);
  // Probe on or_4_out
  or or_6 (or_6_out, or_5_out, dipswitch_4_sw5);
  Multiplexer #(.width(16)) multiplexer_3 (
    .in0(multiplexer_1_out), .in1(multiplexer_2_out), .out(multiplexer_3_out), .sel(in_23));
  or or_7 (or_7_out, or_6_out, dipswitch_4_sw6);
  // Probe on multiplexer_3_out
  or or_8 (or_8_out, or_7_out, dipswitch_4_sw7);
  // Probe on or_9_out
  or or_9 (or_9_out, or_8_out, dipswitch_4_sw8);
  Demultiplexer #(.select(2)) demultiplexer_7 (.in(in_5), .sel(in_6));  // open: out0, out1, out2, out3
  Multiplexer #(.select(3), .width(16)) multiplexer_4 (
    .in0(in_12), .in1(in_13), .in2(in_15), .in3(in_17), .in4(in_19), .in5(in_20), .in6(in_24), .in7(in_26),
    .out(multiplexer_4_out), .sel(in_25));
  // Probe on multiplexer_4_out

  // Notes on the sheet:
  //   MUX
  //   DMUX
  //   DMux4Way
  //   DMux8Way
  //   Mux4Way16
  //   Half adder
  //   OR
  //   XOR
  //   Or8Way
endmodule
